# Fritzing sketch Untitled Sketch (saved by Fritzing 0.9.3b)
breadboards: 1

parts:
  Part1 = Arduino Nano (Rev3.0)
  Part3 = Triple Axis Accelerometer Breakout - ADXL345
  Pololu_A1 = Pololu A4988 [package=SO16]
  Part4 = Logic Level Converter
  BAT1 = Battery Holders [package=battcom_20mm_pth]  # not connected
  C1 = Capacitor Polarized [package=cpol-radial-10uf-25v]

nets:
  GND: Part1.GND, Part3.GND
  N1: Part1.D2, Pololu_A1.1B
  N2: Part1.D3, Pololu_A1.1A
  N3: Part1.D4, Pololu_A1.2B
  N4: Part1.D5, Pololu_A1.2A
  5V: Part1.5V, Part3.VCC
  N5: Part1.A5, Part3.SCL
  N6: Part1.A4, Part3.SDA
  N7: Part4.TX2_LV, Part4.RX2_LV, Part4.GND, Part4.RX2_HV, Part4.TX2_HV
  N8: Part4.TX_LV, C1.-
  N9: Part4.TX_HV, C1.+
